# Fritzing sketch CIT-GardeningAdventure (saved by Fritzing 0.9.5d)
breadboards: 1

parts:
  IC1 = MCP3008 8-channel 10-bit ADC [part_number=MCP3008]
  Raspberry_Pi = Raspberry Pi 3 [part_number=RPI-3-V1.2]
  DHT_22 = DHT22 Humidity and Temperature Sensor
  V1 = DC Power [voltage=5]  # not connected
  Soil_Moisture_Sensor = FC-28 Soil Hygrometer Module - Probe
  부품3 = FC-28 Soil Hygrometer Module
  Water_Level_Sensor = Water Level Sensor
  LDR = Photocell (LDR) [package=THT]
  R2 = Resistor [tolerance=±5% resistance=10k package="2512 [SMD]"]
  R3 = Resistor [tolerance=±5% resistance=10k package="2512 [SMD]"]
  NeoPixel_Ring = 12 NeoPixel Ring [part_number=1643]

nets:
  N1: IC1.no_name_yet#6, LDR.pin_1, R3.Pin_1
  N2: IC1.no_name_yet#7, Water_Level_Sensor.SIG
  N3: IC1.no_name_yet#8, 부품3.AO
  GND: IC1.no_name_yet#9, IC1.no_name_yet#14, Raspberry_Pi.GND, DHT_22.GND, 부품3.GND, Water_Level_Sensor.GND, NeoPixel_Ring.GND
  N4: IC1.no_name_yet#10, Raspberry_Pi.GIPO8
  N5: IC1.no_name_yet#11, Raspberry_Pi.GIPO10
  N6: IC1.no_name_yet#12, Raspberry_Pi.GIPO9
  N7: IC1.no_name_yet#13, Raspberry_Pi.GIPO11
  VDD: IC1.no_name_yet#15, IC1.no_name_yet#16, Raspberry_Pi.5V, DHT_22.VDD, 부품3.VCC, Water_Level_Sensor.VCC, LDR.pin_0, R3.Pin_0, NeoPixel_Ring.VDD
  N8: Raspberry_Pi.GIPO4, R2.Pin_0
  N9: Raspberry_Pi.GIPO18, NeoPixel_Ring.IN
  N10: DHT_22.DATA, R2.Pin_1
  N11: Soil_Moisture_Sensor.POS, 부품3.POS
  N12: Soil_Moisture_Sensor.NEG, 부품3.NEG

custom parts:
  FC-28 Soil Hygrometer Module - Probe: The FC-28 is a soil hygrometer module that uses the Texas Instruments LM393 comparator chip to provide an analog measurement of soil humidity.
  FC-28 Soil Hygrometer Module: The FC-28 is a soil hygrometer module that uses the Texas Instruments LM393 comparator chip to provide an analog measurement of soil humidity. The digital output is high when soil moisture is over a certain threshold, as determined by adjusting the potentiometer.
  Water Level Sensor: A water level sensor. This sensor operates at 3V to 5V. The Sig (signal) pin outputs an analogue signal that is in proportion to the amount of water in contact with the sensor.
  12 NeoPixel Ring: 12 ultra bright smart LED NeoPixels are arranged in a circle with 1.5" (37mm) outer diameter. The rings are 'chainable' - connect the output pin of one to the input pin of another. Use only one microcontroller pin to control as many as you can chain together! Each LED is addressable as the driver chip is inside the LED. Each one has ~18mA constant current drive so the color will be very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
