# Fritzing sketch Wiring Diagram (saved by Fritzing 0.9.3b)
breadboards: 1

parts:
  Raspberry_Pi_1 = Raspberry Pi 3 [part_number=RPI-3-V1.2]
  R1 = Resistor [tolerance=±5% resistance=10k package="2512 [SMD]"]
  DHT22 = DHT22 Humidity and Temperature Sensor
  IC1 = MCP3008 8-channel 10-bit ADC [part_number=MCP3008]
  Water_Level_Sensor = Water Level Sensor
  Soil_Moisture_Sensor = Soil Moisture Sensor
  LDR = Photocell (LDR) [package=THT]
  R2 = Resistor [tolerance=±5% resistance=10k package="2512 [SMD]"]

nets:
  VCC: Raspberry_Pi_1.3v3, R1.Pin_0, IC1.no_name_yet#15, IC1.no_name_yet#16, Water_Level_Sensor.VCC, Soil_Moisture_Sensor.VCC, LDR.pin_1
  N1: Raspberry_Pi_1.GIPO4, R1.Pin_1, DHT22.DATA
  N2: Raspberry_Pi_1.GIPO10, IC1.no_name_yet#11
  N3: Raspberry_Pi_1.GIPO9, IC1.no_name_yet#12
  N4: Raspberry_Pi_1.GIPO11, IC1.no_name_yet#13
  N5: Raspberry_Pi_1.GIPO8, IC1.no_name_yet#10
  GND: Raspberry_Pi_1.GND, DHT22.NULL, DHT22.GND, IC1.no_name_yet#9, IC1.no_name_yet#14, Water_Level_Sensor.GND, Soil_Moisture_Sensor.GND, R2.Pin_1
  N6: IC1.no_name_yet#1, Water_Level_Sensor.SIG
  N7: IC1.no_name_yet#2, Soil_Moisture_Sensor.SIG
  N8: IC1.no_name_yet#3, LDR.pin_0, R2.Pin_0

custom parts:
  Water Level Sensor: A water level sensor. This sensor operates at 3V to 5V. The Sig (signal) pin outputs an analogue signal that is in proportion to the amount of water in contact with the sensor.
